# Fritzing sketch ProjectAuraFritzing (saved by Fritzing 0.9.3b)
breadboards: 1

parts:
  Part1 = Arduino Uno (Rev3)
  LED1 = RGB LED (com. anode, rbg) [package="5 mm [THT]"]
  RF1 = nRF8001 Bluetooth LE Breakout
  Part2 = Adafruit TCS34725 RGB Color Sensor [part_number="Adafruit #1334"]
  R2 = Resistor [tolerance=±5% resistance=220 package="1206 [SMD]"]
  R3 = Resistor [tolerance=±5% resistance=220 package="1206 [SMD]"]
  R4 = Resistor [tolerance=±5% resistance=220 package="1206 [SMD]"]

nets:
  N1: Part1.A4/SDA, Part2.SDA
  N2: Part1.A5/SCL, Part2.SCL
  N3: Part1.D8, RF1.RST
  N4: Part1.D10_PWM/SS, RF1.REQ
  N5: Part1.D11_PWM/MOSI, RF1.MOSI
  N6: Part1.D12/MISO, RF1.MISO
  N7: Part1.D13/SCK, RF1.SCK
  GND: Part1.GND, LED1.common_anode, RF1.GND, Part2.GND
  N8: Part1.D2, RF1.RDY
  N9: Part1.D3_PWM, R2.Pin_1
  N10: Part1.D4, Part2.LED_EN
  N11: Part1.D5_PWM, R3.Pin_1
  N12: Part1.D6_PWM, R4.Pin_1
  VIN: Part1.5V, RF1.VIN, Part2.VIN
  N13: LED1.red_cathode, R4.Pin_0
  N14: LED1.blue_cathode, R3.Pin_0
  N15: LED1.green_cathode, R2.Pin_0

custom parts:
  nRF8001 Bluetooth LE Breakout: nRF8001 Breakout Board
  Adafruit TCS34725 RGB Color Sensor: Your electronics can now see in dazzling color with this lovely color light sensor. We found the best color sensor on the market, the TCS34725, which has RGB and Clear light sensing elements. An IR blocking filter, integrated on-chip and localized to the color sensing photodiodes, minimizes the IR spectral component of the incoming light and allows color measurements to be made accurately. The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
